// Logisim project Lab 7 Circuit - Simplified for Breadboard.circ as structural Verilog: 1 circuit, main circuit main
module main (
  input  H,
  input  L,
  input  R,
  output a,
  output b,
  output c,
  output d,
  output e,
  output f
);

  wire and_1_out, and_2_out, and_3_out, and_4_out, and_5_out, and_6_out, and_7_out, and_8_out, and_9_out,
       and_10_out, and_11_out, and_13_out, and_14_out, and_16_out, clock_1_out, d_ff_1_qn, d_ff_2_q,
       d_ff_2_qn, d_ff_3_q, d_ff_3_qn, not_1_out, or_1_out, or_2_out, or_3_out, or_4_out;

  not not_1 (not_1_out, H);
  // NOT_Gate not_2 has open pins: in=L, out=open
  // NOT_Gate not_3 has open pins: in=R, out=open
  and and_1 (and_1_out, not_1_out, R, d_ff_2_qn);
  and and_2 (and_2_out, not_1_out, L, d_ff_1_qn);
  and and_3 (and_3_out, H, d_ff_1_qn, d_ff_2_qn, d_ff_3_qn);
  and and_4 (and_4_out, d_ff_2_q, d_ff_3_qn);
  and and_5 (and_5_out, d_ff_2_qn, d_ff_3_q);
  or or_1 (or_1_out, and_4_out, and_5_out);
  and and_6 (and_6_out, and_1_out, d_ff_3_qn);
  and and_7 (and_7_out, and_1_out, d);
  and and_8 (and_8_out, and_7_out, d_ff_3_q);
  and and_9 (and_9_out, and_2_out, d_ff_3_qn);
  and and_10 (and_10_out, d_ff_3_qn, and_7_out);
  and and_11 (and_11_out, and_2_out, or_1_out);
  Clock clock_1 (.out(clock_1_out));
  or or_2 (or_2_out, and_6_out, and_7_out, and_3_out);
  or or_3 (or_3_out, and_11_out, and_8_out, and_3_out);
  or or_4 (or_4_out, and_10_out, and_9_out, and_3_out);
  D_Flip_Flop d_ff_1 (.clk(clock_1_out), .D(or_2_out), .Q(d), .Qn(d_ff_1_qn));  // open: preset, en, reset
  D_Flip_Flop d_ff_2 (.clk(clock_1_out), .D(or_3_out), .Q(d_ff_2_q), .Qn(d_ff_2_qn));  // open: preset, en, reset
  D_Flip_Flop d_ff_3 (.clk(clock_1_out), .D(or_4_out), .Q(d_ff_3_q), .Qn(d_ff_3_qn));  // open: preset, en, reset
  and and_12 (a, d_ff_2_q, d_ff_3_q);
  and and_13 (and_13_out, d_ff_1_qn, d_ff_2_q);
  and and_14 (and_14_out, d_ff_1_qn, d_ff_3_q);
  and and_15 (f, d, d_ff_2_q);
  and and_16 (and_16_out, d, d_ff_3_q);
  or or_5 (b, a, and_13_out);
  or or_6 (c, b, and_14_out);
  or or_7 (e, f, and_16_out);

  // Notes on the sheet:
  //   H'
  //   2 Input AND: SN74HC08N
  //   2 INPUT OR: SN74HC32N
  //   D FLIPFLOP: SN74HC74N
  //   4 INPUT AND: SN74HC21N
  //   INVERTER: SN74HC04N
  //   3 INPUT NAND: SN74HC10N
  //   4 INPUT OR: CD4072BE
  //   x
  //   y
  //   z
endmodule
