// Logisim project Lab 7 Circuit - Using Tools.circ as structural Verilog: 3 circuits, main circuit main
module main (
  input  H,
  input  L,
  input  R,
  output a,
  output b,
  output xn,
  output c,
  output d,
  output e,
  output f,
  output yn,
  output zn
);

  wire and_1_out, and_2_out, and_3_out, and_4_out, and_5_out, and_6_out, and_7_out, and_8_out, and_9_out,
       and_10_out, and_13_out, and_14_out, and_15_out, and_16_out, and_17_out, clock_1_out, d_ff_2_q,
       d_ff_3_q, not_1_out, not_2_out, not_3_out, not_4_out, not_5_out, not_6_out, not_7_out, not_8_out,
       not_9_out, not_10_out, not_11_out, not_12_out, not_13_out, not_14_out, not_15_out, not_16_out,
       not_17_out, not_18_out, not_19_out, not_20_out, not_21_out, not_22_out, not_23_out, not_24_out,
       not_25_out, not_26_out, not_27_out, not_28_out, not_29_out, not_30_out, not_31_out, or_4_out;

  not not_1 (not_1_out, H);
  not not_2 (not_2_out, d_ff_2_q);
  not not_3 (not_3_out, d_ff_3_q);
  not not_4 (not_4_out, H);
  not not_5 (not_5_out, d_ff_2_q);
  not not_6 (not_6_out, d);
  not not_7 (not_7_out, d_ff_2_q);
  not not_8 (not_8_out, d_ff_3_q);
  not not_9 (not_9_out, d);
  not not_10 (not_10_out, d_ff_2_q);
  not not_11 (not_11_out, d_ff_3_q);
  not not_12 (not_12_out, H);
  not not_13 (not_13_out, d_ff_2_q);
  not not_14 (not_14_out, H);
  not not_15 (not_15_out, d);
  not not_16 (not_16_out, d_ff_2_q);
  not not_17 (not_17_out, H);
  not not_18 (not_18_out, d);
  not not_19 (not_19_out, d_ff_3_q);
  not not_20 (not_20_out, H);
  not not_21 (not_21_out, d);
  not not_22 (not_22_out, d_ff_3_q);
  not not_23 (not_23_out, d);
  not not_24 (not_24_out, d_ff_2_q);
  not not_25 (not_25_out, d_ff_3_q);
  not not_26 (not_26_out, H);
  not not_27 (not_27_out, d_ff_2_q);
  not not_28 (not_28_out, d_ff_3_q);
  and and_1 (and_1_out, not_1_out, R, not_2_out, not_3_out);
  and and_2 (and_2_out, not_4_out, R, d, not_5_out);
  and and_3 (and_3_out, H, not_6_out, not_7_out, not_8_out);
  and and_4 (and_4_out, H, not_9_out, not_10_out, not_11_out);
  and and_5 (and_5_out, not_12_out, R, d, not_13_out, d_ff_3_q);
  and and_6 (and_6_out, not_14_out, L, not_15_out, not_16_out, d_ff_3_q);
  and and_7 (and_7_out, not_17_out, L, not_18_out, d_ff_2_q, not_19_out);
  and and_8 (and_8_out, not_20_out, L, not_21_out, not_22_out);
  and and_9 (and_9_out, H, not_23_out, not_24_out, not_25_out);
  and and_10 (and_10_out, not_26_out, R, d, not_27_out, not_28_out);
  or or_1 (xn, and_1_out, and_2_out, and_3_out);
  or or_2 (yn, and_4_out, and_5_out, and_6_out, and_7_out);
  or or_3 (zn, and_8_out, and_9_out, and_10_out);
  Clock clock_1 (.out(clock_1_out));
  D_Flip_Flop d_ff_1 (.clk(clock_1_out), .D(xn), .Q(d));  // open: Qn, preset, en, reset
  D_Flip_Flop d_ff_2 (.clk(clock_1_out), .D(yn), .Q(d_ff_2_q));  // open: Qn, preset, en, reset
  D_Flip_Flop d_ff_3 (.clk(clock_1_out), .D(zn), .Q(d_ff_3_q));  // open: Qn, preset, en, reset
  and and_11 (a, d_ff_2_q, d_ff_3_q);
  not not_29 (not_29_out, d);
  not not_30 (not_30_out, d);
  not not_31 (not_31_out, d);
  or or_4 (or_4_out, d_ff_2_q, d_ff_3_q);
  and and_12 (f, d, d_ff_2_q);
  and and_13 (and_13_out, d_ff_2_q, not_29_out);
  and and_14 (and_14_out, d_ff_3_q, d_ff_2_q);
  and and_15 (and_15_out, d_ff_2_q, not_30_out);
  and and_16 (and_16_out, d_ff_3_q, d_ff_2_q);
  and and_17 (and_17_out, d_ff_3_q, not_31_out);
  and and_18 (e, d, or_4_out);
  or or_5 (b, and_13_out, and_14_out);
  or or_6 (c, and_15_out, and_16_out, and_17_out);
endmodule

module Next_State (
  input  H,
  input  L,
  input  R,
  output xn,
  output yn,
  output zn
);

  wire and_1_out, and_2_out, and_3_out, and_4_out, and_5_out, and_6_out, and_7_out, and_8_out, and_9_out,
       and_10_out, clock_1_out, d_ff_1_q, d_ff_2_q, d_ff_3_q, not_1_out, not_2_out, not_3_out, not_4_out,
       not_5_out, not_6_out, not_7_out, not_8_out, not_9_out, not_10_out, not_11_out, not_12_out, not_13_out,
       not_14_out, not_15_out, not_16_out, not_17_out, not_18_out, not_19_out, not_20_out, not_21_out,
       not_22_out, not_23_out, not_24_out, not_25_out, not_26_out, not_27_out, not_28_out;

  not not_1 (not_1_out, H);
  not not_2 (not_2_out, d_ff_2_q);
  not not_3 (not_3_out, d_ff_3_q);
  not not_4 (not_4_out, H);
  not not_5 (not_5_out, d_ff_2_q);
  not not_6 (not_6_out, d_ff_1_q);
  not not_7 (not_7_out, d_ff_2_q);
  not not_8 (not_8_out, d_ff_3_q);
  not not_9 (not_9_out, d_ff_1_q);
  not not_10 (not_10_out, d_ff_2_q);
  not not_11 (not_11_out, d_ff_3_q);
  not not_12 (not_12_out, H);
  not not_13 (not_13_out, d_ff_2_q);
  not not_14 (not_14_out, H);
  not not_15 (not_15_out, d_ff_1_q);
  not not_16 (not_16_out, d_ff_2_q);
  not not_17 (not_17_out, H);
  not not_18 (not_18_out, d_ff_1_q);
  not not_19 (not_19_out, d_ff_3_q);
  not not_20 (not_20_out, H);
  not not_21 (not_21_out, d_ff_1_q);
  not not_22 (not_22_out, d_ff_3_q);
  not not_23 (not_23_out, d_ff_1_q);
  not not_24 (not_24_out, d_ff_2_q);
  not not_25 (not_25_out, d_ff_3_q);
  not not_26 (not_26_out, H);
  not not_27 (not_27_out, d_ff_2_q);
  not not_28 (not_28_out, d_ff_3_q);
  and and_1 (and_1_out, not_1_out, R, not_2_out, not_3_out);
  and and_2 (and_2_out, not_4_out, R, d_ff_1_q, not_5_out);
  and and_3 (and_3_out, H, not_6_out, not_7_out, not_8_out);
  and and_4 (and_4_out, H, not_9_out, not_10_out, not_11_out);
  and and_5 (and_5_out, not_12_out, R, d_ff_1_q, not_13_out, d_ff_3_q);
  and and_6 (and_6_out, not_14_out, L, not_15_out, not_16_out, d_ff_3_q);
  and and_7 (and_7_out, not_17_out, L, not_18_out, d_ff_2_q, not_19_out);
  and and_8 (and_8_out, not_20_out, L, not_21_out, not_22_out);
  and and_9 (and_9_out, H, not_23_out, not_24_out, not_25_out);
  and and_10 (and_10_out, not_26_out, R, d_ff_1_q, not_27_out, not_28_out);
  or or_1 (xn, and_1_out, and_2_out, and_3_out);
  or or_2 (yn, and_4_out, and_5_out, and_6_out, and_7_out);
  or or_3 (zn, and_8_out, and_9_out, and_10_out);
  Clock clock_1 (.out(clock_1_out));
  D_Flip_Flop d_ff_1 (.clk(clock_1_out), .D(xn), .Q(d_ff_1_q));  // open: Qn, preset, en, reset
  D_Flip_Flop d_ff_2 (.clk(clock_1_out), .D(yn), .Q(d_ff_2_q));  // open: Qn, preset, en, reset
  D_Flip_Flop d_ff_3 (.clk(clock_1_out), .D(zn), .Q(d_ff_3_q));  // open: Qn, preset, en, reset
endmodule

module Output_Logic (
  input  x,
  input  y,
  input  z,
  output a,
  output b,
  output c,
  output d,
  output e,
  output f
);

  wire and_3_out, and_4_out, and_5_out, and_6_out, and_7_out, not_1_out, not_2_out, not_3_out, or_1_out;

  and and_1 (a, y, z);
  not not_1 (not_1_out, x);
  not not_2 (not_2_out, x);
  not not_3 (not_3_out, x);
  or or_1 (or_1_out, y, z);
  and and_2 (f, x, y);
  and and_3 (and_3_out, y, not_1_out);
  and and_4 (and_4_out, z, y);
  and and_5 (and_5_out, y, not_2_out);
  and and_6 (and_6_out, z, y);
  and and_7 (and_7_out, z, not_3_out);
  and and_8 (e, x, or_1_out);
  or or_2 (b, and_3_out, and_4_out);
  or or_3 (c, and_5_out, and_6_out, and_7_out);

  assign d = x;
endmodule
